# Fritzing sketch ArduinoBlueToothLedSketch (saved by Fritzing 0.9.3b)
breadboards: 1

parts:
  Part1 = Arduino Uno (Rev3) - ICSP
  Part2 = Bluetooth HC-05 Macho
  LED1 = RGB LED (com. cathode, rgb) [package="5 mm [THT]"]

nets:
  5V: Part1.5V, Part2.VCC
  GND: Part1.GND, Part2.GND, LED1.common_cathode
  N1: Part1.D0/RX, Part2.TXD
  N2: Part1.D1/TX, Part2.RXD
  N3: Part1.D3_PWM, LED1.red_anode
  N4: Part1.D5_PWM, LED1.green_anode
  N5: Part1.D6_PWM, LED1.blue_anode
